# Fritzing sketch Arbetskrav1-v.2 (saved by Fritzing 0.9.10b)
breadboards: 1

parts:
  IC1 = L293D [package=THT]
  Part1 = Arduino Uno (Rev3) - ICSP
  M1 = DC Motor [voltage_(max)=6V voltage_(min)=3V]
  Keypad4x1 = Keypad Membran 4x4
  Mod1 = KY-023 Dual Axis Joystick Module [package="Breakout board"]
  Part2 = Matrix LED de 8x8 basada en MAX7219

nets:
  N1: IC1.Enable_1, Part1.D9_PWM
  N2: IC1.In_1, Part1.A2
  N3: IC1.Out_1_(_Controlled_by_Enable_1_), M1.pin_1
  GND: IC1.0V, Part1.GND, Mod1.GND, Part2.GND
  N4: IC1.Out_2_(_Controlled_by_Enable_1_), M1.pin_2
  N5: IC1.In_2, Part1.A3
  5V: IC1.+Vmotor, IC1.+V, Part1.5V, Mod1.+5V, Part2.VCC
  N6: Part1.A0, Mod1.VRx
  N7: Part1.D8, Keypad4x1.Pin1
  N8: Part1.D10_PWM/SS, Part2.CLK
  N9: Part1.D11_PWM/MOSI, Part2.CS
  N10: Part1.D12/MISO, Part2.DIN
  N11: Part1.D13/SCK, Mod1.SW
  N12: Part1.D2, Keypad4x1.Pin7
  N13: Part1.D3_PWM, Keypad4x1.Pin6
  N14: Part1.D4, Keypad4x1.Pin5
  N15: Part1.D5_PWM, Keypad4x1.Pin4
  N16: Part1.D6_PWM, Keypad4x1.Pin3
  N17: Part1.D7, Keypad4x1.Pin2

custom parts:
  Keypad Membran 4x4: Membrane Keypad 4x4 Matrix
  KY-023 Dual Axis Joystick Module: KY-023 Dual-Axis Joystick Module.
